// Logisim project Project2.circ as structural Verilog: 1 circuit, main circuit main
module main (
  input  C,
  input  A,
  input  B,
  output out_4
);

  wire n7404_1_p2, n7408_1_p3;

  // _7404 7404_1: pin names not known; wires that end beside it: C, n7404_1_p2, 1'b0, 1'b1
  // _7408 7408_1: pin names not known; wires that end beside it: n7404_1_p2, A, n7408_1_p3, 1'b0, 1'b1
  // _7432 7432_1: pin names not known; wires that end beside it: n7408_1_p3, B, out_4, 1'b0, 1'b1

  // Notes on the sheet:
  //   B+AC'
endmodule
