// Logisim project Project3.circ as structural Verilog: 1 circuit, main circuit main
module main (
  input  Y,
  input  Z,
  input  X,
  output out_4
);

  wire n7432_1_p3, n7432_1_p4;

  // _7432 7432_1: pin names not known; wires that end beside it: Y, Z, n7432_1_p3, n7432_1_p4, X, out_4, 1'b0, 1'b1
  // _7404 7404_1: pin names not known; wires that end beside it: n7432_1_p3, n7432_1_p4

  // Notes on the sheet:
  //   X+(Y+Z)'
endmodule
