// Logisim project problem1.circ as structural Verilog: 1 circuit, main circuit main
module main (
  input  A,
  input  C,
  output out_3
);

  wire n7404_1_p2, n7404_1_p4, n7408_1_p3, n7408_1_p6;

  // _7404 7404_1: pin names not known; wires that end beside it: A, n7404_1_p2, C, n7404_1_p4, 1'b0, 1'b1
  // _7408 7408_1: pin names not known; wires that end beside it: n7404_1_p2, n7404_1_p4, n7408_1_p3, C, A, n7408_1_p6, 1'b0, 1'b1
  // _7432 7432_1: pin names not known; wires that end beside it: n7408_1_p3, n7408_1_p6, out_3, 1'b0, 1'b1

  // Notes on the sheet:
  //   AC+A'C'
endmodule
