// Logisim project 2105009.circ as structural Verilog: 1 circuit, main circuit main
module main (
  input  P,
  input  Q,
  input  R,
  output D,
  output B
);

  wire n7404_1_p2, n7408_1_p3, n7408_1_p6, n7408_1_p11, n7432_1_p3, n7486_1_p3;

  // _7486 7486_1: pin names not known; wires that end beside it: P, Q, n7486_1_p3, n7486_1_p3, R, D, 1'b0, 1'b1
  // _7404 7404_1: pin names not known; wires that end beside it: P, n7404_1_p2, 1'b0, 1'b1
  // _7408 7408_1: pin names not known; wires that end beside it: n7404_1_p2, Q, n7408_1_p3, n7404_1_p2, R, n7408_1_p6, 1'b0, 1'b1, R, Q, n7408_1_p11
  // _7432 7432_1: pin names not known; wires that end beside it: n7408_1_p3, n7408_1_p6, n7432_1_p3, n7432_1_p3, n7408_1_p11, B, 1'b0, 1'b1
endmodule
