// Logisim project problem2.circ as structural Verilog: 1 circuit, main circuit main
module main (
  input  A,
  input  C,
  input  D,
  output out_4
);

  wire n7404_1_p2, n7404_1_p4, n7404_1_p6, n7408_1_p3, n7408_1_p6, n7408_1_p11;

  // _7404 7404_1: pin names not known; wires that end beside it: A, n7404_1_p2, C, n7404_1_p4, D, n7404_1_p6, 1'b0, 1'b1
  // _7408 7408_1: pin names not known; wires that end beside it: n7404_1_p2, C, n7408_1_p3, n7408_1_p3, n7404_1_p6, n7408_1_p6, 1'b0, 1'b1, A, n7404_1_p4, n7408_1_p11
  // _7432 7432_1: pin names not known; wires that end beside it: n7408_1_p6, n7408_1_p11, out_4, 1'b0, 1'b1

  // Notes on the sheet:
  //   A'CD'+AC'
endmodule
