// Logisim project COMBINATIONAL_LOGIC.circ as structural Verilog
module CombinationalLogic (
  input  CS2,
  input  CS1,
  input  CS0,
  input  B3,
  input  B2,
  input  B1,
  input  B0,
  input  A3,
  input  A2,
  input  A1,
  input  A0,
  output Z,
  output S,
  output V,
  output C,
  output F3,
  output F2,
  output F1,
  output F0,
  output Y3,
  output Y2,
  output Y1,
  output Y0,
  output X3,
  output X2,
  output X1,
  output X0,
  output out_28,
  output out_29,
  output out_30,
  output out_31
);

  wire n7404_1_p2, n7404_1_p4, n7404_1_p6, n7404_1_p8, n7404_1_p10, n7404_1_p12, n7404_2_p6, n7404_2_p8,
       n7404_2_p10, n7408_1_p8, n7408_1_p10, n7408_1_p11, n7408_2_p3, n7408_2_p8, n7408_2_p9, n7408_2_p10,
       n7408_3_p3, n7408_3_p6, n7408_3_p9, n7432_1_p3, n7432_1_p6, n7432_1_p7, n7432_1_p8, n7483_1_p9,
       n7486_1_p3, n7486_1_p6, n7486_1_p9, n7486_1_p12, n74157_1_p1, n74157_2_p1, n74157_2_p8;

  // _7404 7404_1: pin names not known; wires that end beside it: B3, n7404_1_p2, B2, n7404_1_p4, B1, n7404_1_p6, CS2, n7404_1_p8, CS1, n7404_1_p10, B0, n7404_1_p12
  // _74157 74157_1: pin names not known; wires that end beside it: n74157_1_p1, B0, n7404_1_p12, out_31, B1, n7404_1_p6, out_30, 1'b0, 1'b0, B3, n7404_1_p2, out_28, B2, n7404_1_p4, out_29
  // _7408 7408_1: pin names not known; wires that end beside it: n7404_1_p8, n7404_1_p10, n7404_1_p8, CS1, n74157_1_p1, CS2, CS1, n7408_1_p8, CS0, n7408_1_p10, n7408_1_p11, n7404_1_p10, n7404_1_p8, n7408_1_p10
  // _74157 74157_2: pin names not known; wires that end beside it: n74157_2_p1, out_31, 1'b1, Y0, out_30, 1'b1, Y1, n74157_2_p8, out_28, 1'b1, Y3, out_29, 1'b1, Y2
  // _7432 7432_1: pin names not known; wires that end beside it: n7408_1_p8, n7408_1_p11, n7432_1_p3, F2, CS1, n7432_1_p6, n7432_1_p7, n7432_1_p8, n7432_1_p3, n74157_2_p8
  // _7408 7408_2: pin names not known; wires that end beside it: CS2, n7404_1_p10, n7408_2_p3, n7408_2_p3, CS0, n74157_2_p1, F3, n7408_2_p8, n7408_2_p9, n7408_2_p10, n7432_1_p6, n7408_2_p9, CS2, n7432_1_p8
  // _7486 7486_1: pin names not known; wires that end beside it: A3, B3, n7486_1_p3, A2, B2, n7486_1_p6, A1, B1, n7486_1_p9, A0, B0, n7486_1_p12
  // _7404 7404_2: pin names not known; wires that end beside it: CS0, n7408_2_p9, CS2, n7408_2_p10, n7408_2_p8, n7404_2_p6, F1, n7404_2_p8, F0, n7404_2_p10
  // _7408 7408_3: pin names not known; wires that end beside it: n7408_2_p9, n7404_1_p10, n7408_3_p3, CS2, n7408_3_p3, n7408_3_p6, n7404_2_p6, n7404_2_p8, n7408_3_p9, n7408_3_p9, n7404_2_p10, Z
  // _74157 74157_3: pin names not known; wires that end beside it: n7408_3_p6, A0, n7486_1_p12, X0, A1, n7486_1_p9, X1, 1'b0, A3, n7486_1_p3, X3, A2, n7486_1_p6, X2
  // _7400_lib_7483 7483_1: pin names not known; wires that end beside it: 1'b0, F2, X2, Y2, F1, Y1, X1, 1'b0, n7483_1_p9, n7432_1_p7, Y0, X0, F0
  // _7400_lib_7483 7483_2: pin names not known; wires that end beside it: V, n7483_1_p9, C, C, 1'b0, 1'b0, n7483_1_p9, Y3, X3, F3

  assign S = F3;

  // Notes on the sheet:
  //   CS2'
endmodule

module _7483 (
  input  _1__A4,
  input  _16__B4,
  input  _3__A3,
  input  _4__B3,
  input  _13__Cin,
  input  _5__Vcc,
  input  _12__GND,
  input  _11__B1,
  input  _7__B2,
  input  _10__A1,
  input  _8__A2,
  output _2__S3,
  output _15__S4,
  output _14__Cout,
  output _6__S2,
  output _9__S1
);

  wire and_1_out, and_2_out, and_3_out, and_4_out, and_5_out, and_6_out, and_7_out, and_8_out, and_9_out,
       and_10_out, and_11_out, and_12_out, and_13_out, and_14_out, nand_1_out, nand_2_out, nand_3_out,
       nand_4_out, nor_1_out, nor_2_out, nor_3_out, nor_4_out, nor_6_out, nor_7_out, nor_8_out, not_1_out,
       not_2_out, not_3_out, not_4_out, not_5_out, not_6_out;

  nand nand_1 (nand_1_out, _16__B4, _1__A4);
  nor nor_1 (nor_1_out, _16__B4, _1__A4);
  nand nand_2 (nand_2_out, _4__B3, _3__A3);
  nor nor_2 (nor_2_out, _4__B3, _3__A3);
  nand nand_3 (nand_3_out, _7__B2, _8__A2);
  nor nor_3 (nor_3_out, _7__B2, _8__A2);
  nand nand_4 (nand_4_out, _11__B1, _10__A1);
  nor nor_4 (nor_4_out, _11__B1, _10__A1);
  and and_1 (and_1_out, nor_2_out, nand_1_out);
  and and_2 (and_2_out, nor_3_out, nand_1_out, nand_2_out);
  and and_3 (and_3_out, nor_4_out, nand_1_out, nand_2_out, nand_3_out);
  and and_4 (and_4_out, nand_1_out, nand_2_out, nand_3_out, nand_4_out, not_2_out);
  not not_1 (not_1_out, nor_1_out);
  and and_5 (and_5_out, nor_3_out, nand_2_out);
  and and_6 (and_6_out, nor_4_out, nand_2_out, nand_3_out);
  and and_7 (and_7_out, nand_2_out, nand_3_out, nand_4_out, not_2_out);
  not not_2 (not_2_out, _13__Cin);
  not not_3 (not_3_out, nor_2_out);
  and and_8 (and_8_out, nor_4_out, nand_3_out);
  and and_9 (and_9_out, nand_3_out, nand_4_out, not_2_out);
  not not_4 (not_4_out, nor_3_out);
  and and_10 (and_10_out, nand_4_out, not_2_out);
  not not_5 (not_5_out, nor_4_out);
  not not_6 (not_6_out, not_2_out);
  nor nor_5 (_14__Cout, nor_1_out, and_1_out, and_2_out, and_3_out, and_4_out);
  and and_11 (and_11_out, nand_1_out, not_1_out);
  and and_12 (and_12_out, nand_2_out, not_3_out);
  and and_13 (and_13_out, nand_3_out, not_4_out);
  and and_14 (and_14_out, nand_4_out, not_5_out);
  xor xor_1 (_15__S4, and_11_out, nor_6_out);
  nor nor_6 (nor_6_out, nor_2_out, and_5_out, and_6_out, and_7_out);
  xor xor_2 (_2__S3, and_12_out, nor_7_out);
  nor nor_7 (nor_7_out, nor_3_out, and_8_out, and_9_out);
  xor xor_3 (_6__S2, and_13_out, nor_8_out);
  nor nor_8 (nor_8_out, nor_4_out, and_10_out);
  xor xor_4 (_9__S1, and_14_out, not_6_out);

  // Notes on the sheet:
  //   7483: 4-bit full adder
endmodule
