// Logisim project ALU.circ as structural Verilog: 5 circuits, main circuit main
module main (
);

  ALU_10_bit alu_10_bit_1 ();  // open: Input_1, Input_2, Control, Output, Carry_Out, Zero_Flag, Sign_Flag
  ALU_12_bit alu_12_bit_1 ();  // open: Input_1, Input_2, Control, Output, Carry_Out, Zero_Flag, Sign_Flag
  ALU_16_bit alu_16_bit_1 ();  // open: Input_1, Input_2, Control, Output, Carry_Out, Zero_Flag, Sign_Flag
  ALU_32_bit alu_32_bit_1 ();  // open: Input_1, Input_2, Control, Output, Carry_Out, Zero_Flag, Sign_Flag
endmodule

// ALU_12
module ALU_12_bit (
  input  [11:0] Input_1,
  input  [11:0] Input_2,
  input  [1:0] Control,
  output [11:0] Output,
  output Carry_Out,
  output Zero_Flag,
  output Sign_Flag
);

  wire adder_1_cout, bitfinder_1_found, subtractor_1_bout;
  wire [11:0] adder_1_out, negator_1_out, subtractor_1_out;

  Negator #(.width(12)) negator_1 (.in(Input_1), .out(negator_1_out));
  Adder #(.width(12)) adder_1 (.a(Input_1), .b(Input_2), .out(adder_1_out), .cin(1'b0), .cout(adder_1_cout));
  Subtractor #(.width(12)) subtractor_1 (
    .a(Input_1), .b(Input_2), .out(subtractor_1_out), .bin(1'b0), .bout(subtractor_1_bout));
  Multiplexer #(.select(2), .width(12)) multiplexer_1 (
    .in0(Input_1), .in1(negator_1_out), .in2(adder_1_out), .in3(subtractor_1_out), .out(Output),
    .sel(Control), .en(1'b1));
  Multiplexer #(.select(2)) multiplexer_2 (
    .in0(1'b0), .in1(1'b0), .in2(adder_1_cout), .in3(subtractor_1_bout), .out(Carry_Out), .sel(Control),
    .en(1'b1));
  BitFinder #(.width(12)) bitfinder_1 (.in(Output), .found(bitfinder_1_found));  // open: index
  not not_1 (Zero_Flag, bitfinder_1_found);

  assign Sign_Flag = Output[11];
endmodule

// ALU_32
module ALU_32_bit (
  input  [31:0] Input_1,
  input  [31:0] Input_2,
  input  [1:0] Control,
  output [31:0] Output,
  output Carry_Out,
  output Zero_Flag,
  output Sign_Flag
);

  wire adder_1_cout, bitfinder_1_found, subtractor_1_bout;
  wire [31:0] adder_1_out, negator_1_out, subtractor_1_out;

  Negator #(.width(32)) negator_1 (.in(Input_1), .out(negator_1_out));
  Adder #(.width(32)) adder_1 (.a(Input_1), .b(Input_2), .out(adder_1_out), .cin(1'b0), .cout(adder_1_cout));
  Subtractor #(.width(32)) subtractor_1 (
    .a(Input_1), .b(Input_2), .out(subtractor_1_out), .bin(1'b0), .bout(subtractor_1_bout));
  Multiplexer #(.select(2), .width(32)) multiplexer_1 (
    .in0(Input_1), .in1(negator_1_out), .in2(adder_1_out), .in3(subtractor_1_out), .out(Output),
    .sel(Control), .en(1'b1));
  Multiplexer #(.select(2)) multiplexer_2 (
    .in0(1'b0), .in1(1'b0), .in2(adder_1_cout), .in3(subtractor_1_bout), .out(Carry_Out), .sel(Control),
    .en(1'b1));
  BitFinder #(.width(32)) bitfinder_1 (.in(Output), .found(bitfinder_1_found));  // open: index
  not not_1 (Zero_Flag, bitfinder_1_found);

  assign Sign_Flag = Output[31];
endmodule

// ALU_10
module ALU_10_bit (
  input  [9:0] Input_1,
  input  [9:0] Input_2,
  input  [1:0] Control,
  output [9:0] Output,
  output Carry_Out,
  output Zero_Flag,
  output Sign_Flag
);

  wire adder_1_cout, bitfinder_1_found, subtractor_1_bout;
  wire [9:0] adder_1_out, negator_1_out, subtractor_1_out;

  Negator #(.width(10)) negator_1 (.in(Input_1), .out(negator_1_out));
  Adder #(.width(10)) adder_1 (.a(Input_1), .b(Input_2), .out(adder_1_out), .cin(1'b0), .cout(adder_1_cout));
  Subtractor #(.width(10)) subtractor_1 (
    .a(Input_1), .b(Input_2), .out(subtractor_1_out), .bin(1'b0), .bout(subtractor_1_bout));
  Multiplexer #(.select(2), .width(10)) multiplexer_1 (
    .in0(Input_1), .in1(negator_1_out), .in2(adder_1_out), .in3(subtractor_1_out), .out(Output),
    .sel(Control), .en(1'b1));
  Multiplexer #(.select(2)) multiplexer_2 (
    .in0(1'b0), .in1(1'b0), .in2(adder_1_cout), .in3(subtractor_1_bout), .out(Carry_Out), .sel(Control),
    .en(1'b1));
  BitFinder #(.width(10)) bitfinder_1 (.in(Output), .found(bitfinder_1_found));  // open: index
  not not_1 (Zero_Flag, bitfinder_1_found);

  assign Sign_Flag = Output[9];
endmodule

// ALU_16
module ALU_16_bit (
  input  [15:0] Input_1,
  input  [15:0] Input_2,
  input  [1:0] Control,
  output [15:0] Output,
  output Carry_Out,
  output Zero_Flag,
  output Sign_Flag
);

  wire adder_1_cout, bitfinder_1_found, subtractor_1_bout;
  wire [15:0] adder_1_out, negator_1_out, subtractor_1_out;

  Negator #(.width(16)) negator_1 (.in(Input_1), .out(negator_1_out));
  Adder #(.width(16)) adder_1 (.a(Input_1), .b(Input_2), .out(adder_1_out), .cin(1'b0), .cout(adder_1_cout));
  Subtractor #(.width(16)) subtractor_1 (
    .a(Input_1), .b(Input_2), .out(subtractor_1_out), .bin(1'b0), .bout(subtractor_1_bout));
  Multiplexer #(.select(2), .width(16)) multiplexer_1 (
    .in0(Input_1), .in1(negator_1_out), .in2(adder_1_out), .in3(subtractor_1_out), .out(Output),
    .sel(Control), .en(1'b1));
  Multiplexer #(.select(2)) multiplexer_2 (
    .in0(1'b0), .in1(1'b0), .in2(adder_1_cout), .in3(subtractor_1_bout), .out(Carry_Out), .sel(Control),
    .en(1'b1));
  BitFinder #(.width(16)) bitfinder_1 (.in(Output), .found(bitfinder_1_found));  // open: index
  not not_1 (Zero_Flag, bitfinder_1_found);

  assign Sign_Flag = Output[15];
endmodule
