// Logisim project Denorm.circ as structural Verilog: 2 circuits, main circuit main
module main (
);

  Denorm denorm_1 ();  // open: Fraction, Exponent, Denormalized
endmodule

// Dnrm
module Denorm (
  input  [31:0] Fraction,
  input  [8:0] Exponent,
  output Denormalized
);

  wire alu_16_bit_1_zero_flag, priority_encoder_32x5_1_valid_bit;
  wire [0:0] comparator_9_bit_1_x_y;
  wire [4:0] comparator_9_bit_1_difference, priority_encoder_32x5_1_a0;

  Priority_Encoder_32x5 priority_encoder_32x5_1 (
    .in_1(Fraction), .Valid_Bit(priority_encoder_32x5_1_valid_bit), .A4(priority_encoder_32x5_1_a0[4]),
    .A3(priority_encoder_32x5_1_a0[3]), .A2(priority_encoder_32x5_1_a0[2]),
    .A1(priority_encoder_32x5_1_a0[1]), .A0(priority_encoder_32x5_1_a0[0]));
  Comparator_9_bit comparator_9_bit_1 (
    .X({4'b0000, priority_encoder_32x5_1_a0}), .Y(9'h1e), .X_Y(comparator_9_bit_1_x_y[0]),
    .DIFFERENCE(comparator_9_bit_1_difference));  // open: SMALLER, LARGER
  ALU_16_bit alu_16_bit_1 (
    .Input_1({{7{1'b0}}, Exponent}), .Input_2({{11{1'b0}}, comparator_9_bit_1_difference}),
    .Control({1'b1, comparator_9_bit_1_x_y[0]}), .Zero_Flag(alu_16_bit_1_zero_flag));  // open: Output, Carry_Out, Sign_Flag
  // _7408 7408_1: pin names not known; wires that end beside it: priority_encoder_32x5_1_valid_bit, alu_16_bit_1_zero_flag, Denormalized, 1'b0, 1'b1
endmodule
