// Logisim project FPA.circ as structural Verilog: 2 circuits, main circuit FPA
module FPA (
  input  [31:0] Input_2,
  input  [31:0] Input_1,
  output Denormalized_Input_1,
  output Denormalized_Input_2,
  output NaN_Input_1,
  output NaN_Input_2,
  output Overflow,
  output Underflow,
  output Denormalized,
  output [31:0] Output,
  output NaN,
  output infinity
);

  wire comparator_fraction_1_out_12, comparator_fraction_1_out_13, n7486_1_p3, n7486_1_p5,
       normalizer_1_overflow, normalizer_1_underflow, normalizer_2_overflow, normalizer_2_underflow;
  wire [4:0] comparator_fraction_1_difference;
  wire [8:0] comparator_fraction_1_common_exponent, normalizer_1_normalized_exponent;
  wire [9:0] shifter_2_out;
  wire [31:0] Adder_Subtractor_result, comparator_fraction_1_largerfraction,
       comparator_fraction_1_smallerfraction, input_validator_1_valid_fraction_1,
       input_validator_1_valid_fraction_2, normalizer_1_normalized_fraction,
       normalizer_2_normalized_fraction, rounder_1_out_2, shifter_1_out;

  Input_Validator input_validator_1 (
    .Fraction_1({2'b01, Input_1[21:0], {8{1'b0}}}), .Exponent_1(Input_1[30:22]),
    .Fraction_2({2'b01, Input_2[21:0], {8{1'b0}}}), .EXponent_2(Input_2[30:22]),
    .Denormalized_Input_1(Denormalized_Input_1), .Denormalized_Input_2(Denormalized_Input_2),
    .NaN_Input_1(NaN_Input_1), .NaN_Input_2(NaN_Input_2),
    .Valid_Fraction_1(input_validator_1_valid_fraction_1),
    .Valid_Fraction_2(input_validator_1_valid_fraction_2));
  Comparator_Fraction comparator_fraction_1 (
    .X_fraction(input_validator_1_valid_fraction_1), .Y_fraction(input_validator_1_valid_fraction_2),
    .X(Input_1[30:22]), .Y(Input_2[30:22]), .X_Sign(Input_1[31]), .Y_Sign(Input_2[31]),
    .LargerFraction(comparator_fraction_1_largerfraction),
    .SmallerFraction(comparator_fraction_1_smallerfraction),
    .Common_Exponent(comparator_fraction_1_common_exponent), .Difference(comparator_fraction_1_difference),
    .out_12(comparator_fraction_1_out_12), .out_13(comparator_fraction_1_out_13));  // open: X_Y
  Shifter #(.width(32), .shift("lr")) shifter_1 (
    .in(comparator_fraction_1_smallerfraction), .\dist (comparator_fraction_1_difference), .out(shifter_1_out));
  Adder_Subtractor Adder_Subtractor (
    .X(comparator_fraction_1_largerfraction), .Y(shifter_1_out), .SignBit1(comparator_fraction_1_out_12),
    .SignBit2(comparator_fraction_1_out_13), .Sign_of_Result(Output[31]), .Result(Adder_Subtractor_result));
  Normalizer normalizer_1 (
    .Fraction(Adder_Subtractor_result), .Exponent(comparator_fraction_1_common_exponent),
    .Normalized_Fraction(normalizer_1_normalized_fraction),
    .Normalized_Exponent(normalizer_1_normalized_exponent), .Overflow(normalizer_1_overflow),
    .Underflow(normalizer_1_underflow));
  // _7486 7486_1: pin names not known; wires that end beside it: normalizer_1_overflow, normalizer_1_underflow, n7486_1_p3, normalizer_1_underflow, n7486_1_p5
  Rounder rounder_1 (.Normalized_Input(normalizer_1_normalized_fraction), .out_2(rounder_1_out_2));
  Normalizer normalizer_2 (
    .Fraction(rounder_1_out_2), .Exponent(normalizer_1_normalized_exponent),
    .Normalized_Fraction(normalizer_2_normalized_fraction), .Normalized_Exponent(Output[30:22]),
    .Overflow(normalizer_2_overflow), .Underflow(normalizer_2_underflow));
  // _74157 74157_1: pin names not known; wires that end beside it: n7486_1_p3, normalizer_2_overflow, normalizer_1_overflow, Overflow, normalizer_2_underflow, 1'b0
  Denorm denorm_1 (
    .Fraction(Adder_Subtractor_result), .Exponent(comparator_fraction_1_common_exponent),
    .Denormalized(Denormalized));
  Shifter #(.width(32)) shifter_2 (
    .in(normalizer_2_normalized_fraction), .\dist (5'b00010), .out({Output[21:0], shifter_2_out}));
  xor xor_1 (Underflow, n7486_1_p5, Denormalized);
  Input_Validator input_validator_2 (
    .Fraction_1({Output[21:0], shifter_2_out}), .Exponent_1(Output[30:22]), .NaN_Input_1(NaN));  // open: Fraction_2, EXponent_2, Denormalized_Input_1, Denormalized_Input_2, NaN_Input_2, Valid_Fraction_1, Valid_Fraction_2
  INF_checker inf_checker_1 (
    .Fraction({Output[21:0], shifter_2_out}), .Exponent(Output[30:22]), .infinity(infinity));  // open: Valid_Fraction
endmodule

module main (
);

  FPA fpa_1 ();  // open: Input_2, Input_1, Denormalized_Input_1, Denormalized_Input_2, NaN_Input_1, NaN_Input_2, Overflow, Underflow, Denormalized, Output, NaN, infinity
endmodule
