// Logisim project INF.circ as structural Verilog
module main (
);

  INF_checker inf_checker_1 ();  // open: Fraction, Exponent, infinity, Valid_Fraction
endmodule

// INF
module INF_checker (
  input  [31:0] Fraction,
  input  [8:0] Exponent,
  output infinity,
  output [31:0] Valid_Fraction
);

  wire alu_10_bit_1_zero_flag, not_1_out, priority_encoder_10x4_1_valid_bit,
       priority_encoder_32x5_1_valid_bit;
  wire [31:0] shifter_1_out;

  Shifter #(.width(32)) shifter_1 (.in(Fraction), .\dist (5'b00010), .out(shifter_1_out));
  Priority_Encoder_32x5 priority_encoder_32x5_1 (
    .in_1(shifter_1_out), .Valid_Bit(priority_encoder_32x5_1_valid_bit));  // open: A4, A3, A2, A1, A0
  Priority_Encoder_10x4 priority_encoder_10x4_1 (
    .in_1({1'b0, Exponent}), .Valid_Bit(priority_encoder_10x4_1_valid_bit));  // open: A3, A2, A1, A0
  ALU_10_bit alu_10_bit_1 (
    .Input_1({10{1'b1}}), .Input_2({1'b1, Exponent}), .Control(2'b11), .Zero_Flag(alu_10_bit_1_zero_flag));  // open: Output, Carry_Out, Sign_Flag
  MUX_32_bit mux_32_bit_1 (
    .X({32{1'b0}}), .Y(Fraction), .Selection(priority_encoder_10x4_1_valid_bit), .Output(Valid_Fraction));
  not not_1 (not_1_out, priority_encoder_32x5_1_valid_bit);
  and and_1 (infinity, alu_10_bit_1_zero_flag, not_1_out);
endmodule
