// Logisim project Rounder.circ as structural Verilog: 2 circuits, main circuit Rounder
module Rounder (
  input  [31:0] Normalized_Input,
  output [31:0] out_2
);

  wire n7432_1_p3, n7432_1_p6, n7432_1_p10, n7432_1_p11, n7432_2_p1, n7432_2_p3, n7432_2_p6;
  wire [0:0] n7408_1_p4;
  wire [31:24] alu_32_bit_1_output;

  // _7432 7432_1: pin names not known; wires that end beside it: Normalized_Input[3], Normalized_Input[4], n7432_1_p3, n7432_1_p3, Normalized_Input[5], n7432_1_p6, 1'b0, 1'b1, Normalized_Input[2], n7432_1_p10, n7432_1_p11, Normalized_Input[1], n7432_1_p6, n7432_1_p10
  // _7432 7432_2: pin names not known; wires that end beside it: n7432_2_p1, Normalized_Input[8], n7432_2_p3, n7432_2_p3, Normalized_Input[6], n7432_2_p6, 1'b1
  // _7408 7408_1: pin names not known; wires that end beside it: 1'b0, n7432_2_p6, Normalized_Input[7], n7408_1_p4[0], 1'b0, 1'b1
  // _7432 7432_3: pin names not known; wires that end beside it: Normalized_Input[0], n7432_1_p11, n7432_2_p1, 1'b0, 1'b1
  ALU_32_bit alu_32_bit_1 (
    .Input_1({{8{1'b0}}, Normalized_Input[31:8]}), .Input_2({{31{1'b0}}, n7408_1_p4[0]}), .Control(2'b10),
    .Output({alu_32_bit_1_output, out_2[31:8]}));  // open: Carry_Out, Zero_Flag, Sign_Flag

  assign out_2[7:0] = {8{1'b0}};
endmodule

module main (
);

  Rounder Rndr ();  // open: Normalized_Input, out_2
endmodule
