// Logisim project Branch Hazard.circ as structural Verilog: 2 circuits, main circuit main
module main (
);

  Branch_Hazard branch_hazard_1 ();  // open: IF_ID_Src_Reg_1, IF_ID_BQE, IF_ID_BNE, ID_EX_Des_Reg, EX_Mem_Des_Reg, IF_ID_Src_Reg_2, Forward_A1, Forward_A0, Branch_Stall, Forward_B1, Forward_B0
endmodule

module Branch_Hazard (
  input  [3:0] IF_ID_Src_Reg_1,
  input  IF_ID_BQE,
  input  IF_ID_BNE,
  input  [3:0] ID_EX_Des_Reg,
  input  [3:0] EX_Mem_Des_Reg,
  input  [3:0] IF_ID_Src_Reg_2,
  output Forward_A1,
  output Forward_A0,
  output Branch_Stall,
  output Forward_B1,
  output Forward_B0
);

  wire and_3_out, and_4_out, comparator_1_eq, comparator_2_eq, comparator_3_eq, comparator_4_eq, not_1_out,
       not_2_out, or_1_out;

  or or_1 (or_1_out, IF_ID_BQE, IF_ID_BNE);
  Comparator #(.width(4), .mode("unsigned")) comparator_1 (
    .a(EX_Mem_Des_Reg), .b(IF_ID_Src_Reg_1), .eq(comparator_1_eq));  // open: gt, lt
  Comparator #(.width(4), .mode("unsigned")) comparator_2 (
    .a(IF_ID_Src_Reg_1), .b(ID_EX_Des_Reg), .eq(comparator_2_eq));  // open: gt, lt
  Comparator #(.width(4), .mode("unsigned")) comparator_3 (
    .a(ID_EX_Des_Reg), .b(IF_ID_Src_Reg_2), .eq(comparator_3_eq));  // open: gt, lt
  Comparator #(.width(4), .mode("unsigned")) comparator_4 (
    .a(EX_Mem_Des_Reg), .b(IF_ID_Src_Reg_2), .eq(comparator_4_eq));  // open: gt, lt
  and and_1 (Forward_A1, comparator_2_eq, or_1_out);
  and and_2 (Forward_B1, or_1_out, comparator_3_eq);
  and and_3 (and_3_out, comparator_1_eq, or_1_out);
  and and_4 (and_4_out, or_1_out, comparator_4_eq);
  not not_1 (not_1_out, Forward_A1);
  and and_5 (Forward_A0, not_1_out, and_3_out);
  not not_2 (not_2_out, Forward_B1);
  and and_6 (Forward_B0, not_2_out, and_4_out);
  or or_2 (Branch_Stall, Forward_A0, Forward_A1, Forward_B0, Forward_B1);
endmodule
