// Logisim project DataMem.circ as structural Verilog: 2 circuits, main circuit main
module main (
);

  DataMem datamem_1 ();  // open: Address, WriteData, MW, MR, Clear, CLK, out_7
endmodule

// Data Mem
module DataMem (
  input  [7:0] Address,
  input  [7:0] WriteData,
  input  MW,
  input  MR,
  input  Clear,
  input  CLK,
  output [7:0] out_7
);

  wire not_1_out;

  not not_1 (not_1_out, CLK);
  RAM #(.bus("separate")) ram_1 (
    .addr(Address), .din(WriteData), .data(out_7), .str(MW), .sel(1'b1), .clk(not_1_out), .ld(MR), .clr(Clear));
endmodule
