// Logisim project EX-MEM.circ as structural Verilog: 1 circuit, main circuit main
module main (
  input  Enable_Register,
  input  [7:0] PC_inp,
  input  [7:0] Branch_inp,
  input  jump_inp,
  input  [7:0] Target_inp,
  input  MTR_inp,
  input  RW_inp,
  input  Bneq_in,
  input  Beq_in,
  input  MW_in,
  input  MR_in,
  input  Zero_in,
  input  [7:0] Result_inp,
  input  [7:0] Write_Data_inp,
  input  [3:0] Des_Reg_inp,
  input  sp_in,
  input  CLK,
  input  CLR,
  output [7:0] PC_out,
  output [7:0] Branch_out,
  output jump_out,
  output [7:0] Target_out,
  output MTR_out,
  output RW_out,
  output Bneq_out,
  output Beq_out,
  output MW_out,
  output MR_out,
  output Zero_out,
  output [7:0] Result_out,
  output [7:0] Write_Data_out,
  output [3:0] Des_Reg_out,
  output sp_out
);

  Register PC_Address (.D(PC_inp), .en(Enable_Register), .Q(PC_out), .clk(CLK), .clr(CLR));
  Register Branch_Address (.D(Branch_inp), .en(Enable_Register), .Q(Branch_out), .clk(CLK), .clr(CLR));
  Register #(.width(1)) jump (.D(jump_inp), .en(Enable_Register), .Q(jump_out), .clk(CLK), .clr(CLR));
  Register Target_Address (.D(Target_inp), .en(Enable_Register), .Q(Target_out), .clk(CLK), .clr(CLR));
  Register #(.width(1)) MTR (.D(MTR_inp), .en(Enable_Register), .Q(MTR_out), .clk(CLK), .clr(CLR));
  Register #(.width(1)) RW (.D(RW_inp), .en(Enable_Register), .Q(RW_out), .clk(CLK), .clr(CLR));
  Register #(.width(1)) BNEQ (.D(Bneq_in), .en(Enable_Register), .Q(Bneq_out), .clk(CLK), .clr(CLR));
  Register #(.width(1)) Beq (.D(Beq_in), .en(Enable_Register), .Q(Beq_out), .clk(CLK), .clr(CLR));
  Register #(.width(1)) MW (.D(MW_in), .en(Enable_Register), .Q(MW_out), .clk(CLK), .clr(CLR));
  Register #(.width(1)) MR (.D(MR_in), .en(Enable_Register), .Q(MR_out), .clk(CLK), .clr(CLR));
  Register #(.width(1)) Zero (.D(Zero_in), .en(Enable_Register), .Q(Zero_out), .clk(CLK), .clr(CLR));
  Register Result (.D(Result_inp), .en(Enable_Register), .Q(Result_out), .clk(CLK), .clr(CLR));
  Register Write_Data (.D(Write_Data_inp), .en(Enable_Register), .Q(Write_Data_out), .clk(CLK), .clr(CLR));
  Register #(.width(4)) Des_reg (.D(Des_Reg_inp), .en(Enable_Register), .Q(Des_Reg_out), .clk(CLK), .clr(CLR));
  Register #(.width(1)) sp (.D(sp_in), .en(Enable_Register), .Q(sp_out), .clk(CLK), .clr(CLR));
endmodule
