// Logisim project Forwarding Unit.circ as structural Verilog: 2 circuits, main circuit main
module main (
  input  [3:0] in_1,
  input  [3:0] in_2,
  input  [3:0] in_3,
  input  [3:0] in_4,
  output [1:0] out_5,
  output [1:0] out_6
);

  Forwarding_Unit forwarding_unit_1 (
    .ID_EX_Src_Reg_1(in_2), .EX_Mem_Reg_Write(1'b0), .EX_Mem_Des_Reg(in_1), .Mem_WB_Des_Reg(in_3),
    .Mem_WB_Reg_Write(1'b1), .ID_EX_Src_Reg_2(in_4), .ForwardA(out_5), .ForwardB(out_6));
endmodule

module Forwarding_Unit (
  input  [3:0] ID_EX_Src_Reg_1,
  input  EX_Mem_Reg_Write,
  input  [3:0] EX_Mem_Des_Reg,
  input  [3:0] Mem_WB_Des_Reg,
  input  Mem_WB_Reg_Write,
  input  [3:0] ID_EX_Src_Reg_2,
  output [1:0] ForwardA,
  output [1:0] ForwardB
);

  wire and_3_out, and_4_out, comparator_1_eq, comparator_2_eq, comparator_3_gt, comparator_4_gt,
       comparator_5_eq, comparator_6_eq, not_1_out, not_2_out;

  Comparator #(.width(4), .mode("unsigned")) comparator_1 (
    .a(Mem_WB_Des_Reg), .b(ID_EX_Src_Reg_1), .eq(comparator_1_eq));  // open: gt, lt
  Comparator #(.width(4), .mode("unsigned")) comparator_2 (
    .a(ID_EX_Src_Reg_1), .b(EX_Mem_Des_Reg), .eq(comparator_2_eq));  // open: gt, lt
  Comparator #(.width(4), .mode("unsigned")) comparator_3 (
    .a(Mem_WB_Des_Reg), .b(4'b0000), .gt(comparator_3_gt));  // open: eq, lt
  Comparator #(.width(4), .mode("unsigned")) comparator_4 (
    .a(EX_Mem_Des_Reg), .b(4'b0000), .gt(comparator_4_gt));  // open: eq, lt
  Comparator #(.width(4), .mode("unsigned")) comparator_5 (
    .a(EX_Mem_Des_Reg), .b(ID_EX_Src_Reg_2), .eq(comparator_5_eq));  // open: gt, lt
  Comparator #(.width(4), .mode("unsigned")) comparator_6 (
    .a(Mem_WB_Des_Reg), .b(ID_EX_Src_Reg_2), .eq(comparator_6_eq));  // open: gt, lt
  and and_1 (ForwardA[1], comparator_2_eq, EX_Mem_Reg_Write, comparator_4_gt);
  and and_2 (ForwardB[1], EX_Mem_Reg_Write, comparator_4_gt, comparator_5_eq);
  and and_3 (and_3_out, comparator_1_eq, comparator_3_gt, Mem_WB_Reg_Write);
  and and_4 (and_4_out, comparator_3_gt, Mem_WB_Reg_Write, comparator_6_eq);
  not not_1 (not_1_out, ForwardA[1]);
  and and_5 (ForwardA[0], not_1_out, and_3_out);
  not not_2 (not_2_out, ForwardB[1]);
  and and_6 (ForwardB[0], not_2_out, and_4_out);
endmodule
