// Logisim project ID-EX.circ as structural Verilog: 2 circuits, main circuit main
module main (
);

  ID_EX id_ex_1 ();  // open: PC_input, Target_Address_inp, ALU_src_inp, MTR_in, RW_in, BNEQ_in, BEQ_in, MW_in, MR_in, jump_in, shift_in, Data_1_inp, Data_2_inp, SRC_Reg_1_inp, Src_Reg_2_inp, Address_inp, Shift_amt_inp, Des_Reg_inp, sp_in, PC_output, Target_Address_Output, ALUop, ALUSrc, MemToReg, RegWrite, bneq, beq, MemWrite, MemRead, jump, shiftAmnt, Data_1_out, Data_2_out, Src_Reg_1_out, Src_Reg_2_out, Addr_Imme, Shift_amt_out, Des_Reg_out, sp, Enable_operation, CLK, CLR, ALU_op_in
endmodule

module ID_EX (
  input  Enable_operation,
  input  [7:0] PC_input,
  input  [7:0] Target_Address_inp,
  input  [2:0] ALU_op_in,
  input  ALU_src_inp,
  input  MTR_in,
  input  RW_in,
  input  BNEQ_in,
  input  BEQ_in,
  input  MW_in,
  input  MR_in,
  input  jump_in,
  input  shift_in,
  input  [7:0] Data_1_inp,
  input  [7:0] Data_2_inp,
  input  [3:0] SRC_Reg_1_inp,
  input  [3:0] Src_Reg_2_inp,
  input  [7:0] Address_inp,
  input  [7:0] Shift_amt_inp,
  input  [3:0] Des_Reg_inp,
  input  sp_in,
  input  CLK,
  input  CLR,
  output [7:0] PC_output,
  output [7:0] Target_Address_Output,
  output [2:0] ALUop,
  output ALUSrc,
  output MemToReg,
  output RegWrite,
  output bneq,
  output beq,
  output MemWrite,
  output MemRead,
  output jump,
  output shiftAmnt,
  output [7:0] Data_1_out,
  output [7:0] Data_2_out,
  output [3:0] Src_Reg_1_out,
  output [3:0] Src_Reg_2_out,
  output [7:0] Addr_Imme,
  output [7:0] Shift_amt_out,
  output [3:0] Des_Reg_out,
  output sp
);

  Register register_1 (.D(PC_input), .en(Enable_operation), .Q(PC_output), .clk(CLK), .clr(CLR));
  Register Target_Address (
    .D(Target_Address_inp), .en(Enable_operation), .Q(Target_Address_Output), .clk(CLK), .clr(CLR));
  Register #(.width(3)) ALU_OP (.D(ALU_op_in), .en(Enable_operation), .Q(ALUop), .clk(CLK), .clr(CLR));
  Register #(.width(1)) ALU_src (.D(ALU_src_inp), .en(Enable_operation), .Q(ALUSrc), .clk(CLK), .clr(CLR));
  Register #(.width(1)) MTR (.D(MTR_in), .en(Enable_operation), .Q(MemToReg), .clk(CLK), .clr(CLR));
  Register #(.width(1)) RW (.D(RW_in), .en(Enable_operation), .Q(RegWrite), .clk(CLK), .clr(CLR));
  Register #(.width(1)) u_BNEQ (.D(BNEQ_in), .en(Enable_operation), .Q(bneq), .clk(CLK), .clr(CLR));
  Register #(.width(1)) u_BEQ (.D(BEQ_in), .en(Enable_operation), .Q(beq), .clk(CLK), .clr(CLR));
  Register #(.width(1)) MW (.D(MW_in), .en(Enable_operation), .Q(MemWrite), .clk(CLK), .clr(CLR));
  Register #(.width(1)) MR (.D(MR_in), .en(Enable_operation), .Q(MemRead), .clk(CLK), .clr(CLR));
  Register #(.width(1)) u_jump (.D(jump_in), .en(Enable_operation), .Q(jump), .clk(CLK), .clr(CLR));
  Register #(.width(1)) shift (.D(shift_in), .en(Enable_operation), .Q(shiftAmnt), .clk(CLK), .clr(CLR));
  Register Data_1 (.D(Data_1_inp), .en(Enable_operation), .Q(Data_1_out), .clk(CLK), .clr(CLR));
  Register Data_2 (.D(Data_2_inp), .en(Enable_operation), .Q(Data_2_out), .clk(CLK), .clr(CLR));
  Register #(.width(4)) Src_Reg_1 (.D(SRC_Reg_1_inp), .en(Enable_operation), .Q(Src_Reg_1_out), .clk(CLK), .clr(CLR));
  Register #(.width(4)) Src_Reg_2 (.D(Src_Reg_2_inp), .en(Enable_operation), .Q(Src_Reg_2_out), .clk(CLK), .clr(CLR));
  Register Address_Immediate (.D(Address_inp), .en(Enable_operation), .Q(Addr_Imme), .clk(CLK), .clr(CLR));
  Register Data_2_2 (.D(Shift_amt_inp), .en(Enable_operation), .Q(Shift_amt_out), .clk(CLK), .clr(CLR));
  Register #(.width(4)) Des_Reg (.D(Des_Reg_inp), .en(Enable_operation), .Q(Des_Reg_out), .clk(CLK), .clr(CLR));
  Register #(.width(1)) u_sp (.D(sp_in), .en(Enable_operation), .Q(sp), .clk(CLK), .clr(CLR));
endmodule
