// Logisim project IF-ID.circ as structural Verilog: 1 circuit, main circuit main
module main (
  input  [7:0] PC_input,
  input  [19:0] Mips_Instructions,
  input  Enable_Change,
  input  CLK,
  input  CLR,
  output [7:0] PC_output,
  output [19:0] Mips_Instructions_Output
);

  Register register_1 (.D(PC_input), .en(Enable_Change), .Q(PC_output), .clk(CLK), .clr(CLR));
  Register #(.width(20)) register_2 (
    .D(Mips_Instructions), .en(Enable_Change), .Q(Mips_Instructions_Output), .clk(CLK), .clr(CLR));
endmodule
