// Logisim project Instruction Splitter.circ as structural Verilog: 2 circuits, main circuit main
module main (
);

  wire [3:0] instructionsplitter_1_dst_reg, instructionsplitter_1_shiftamnt, instructionsplitter_1_src_reg_2;
  wire [19:0] undriven;

  InstructionSplitter instructionsplitter_1 (
    .in_1(undriven), .ShiftAmnt(instructionsplitter_1_shiftamnt), .Dst_Reg(instructionsplitter_1_dst_reg),
    .Src_Reg_2(instructionsplitter_1_src_reg_2));  // open: Src_Reg_1, OpCode, Address___imme, Target_Jump_addr
endmodule

// InsSplitter
module InstructionSplitter (
  input  [19:0] in_1,
  output [3:0] ShiftAmnt,
  output [3:0] Dst_Reg,
  output [3:0] Src_Reg_2,
  output [3:0] Src_Reg_1,
  output [3:0] OpCode,
  output [7:0] Address___imme,
  output [7:0] Target_Jump_addr
);


  assign Address___imme = in_1[7:0];
  assign Dst_Reg = in_1[7:4];
  assign OpCode = in_1[19:16];
  assign ShiftAmnt = in_1[3:0];
  assign Src_Reg_1 = in_1[15:12];
  assign Src_Reg_2 = in_1[11:8];
  assign Target_Jump_addr = in_1[15:8];
endmodule
