// Logisim project Load-Store-Hazard.circ as structural Verilog: 2 circuits, main circuit main
module main (
);

  Load_Store_Hazard load_store_hazard_1 ();  // open: EX_Mem_MW, Ex_Mem_Des_Reg, Mem_WB_Des_Reg, Mem_WB_MR, Load_Store_Hazard
endmodule

module Load_Store_Hazard (
  input  EX_Mem_MW,
  input  [3:0] Ex_Mem_Des_Reg,
  input  [3:0] Mem_WB_Des_Reg,
  input  Mem_WB_MR,
  output Load_Store_Hazard
);

  wire comparator_1_eq, comparator_2_gt;

  Comparator #(.width(4), .mode("unsigned")) comparator_1 (
    .a(Ex_Mem_Des_Reg), .b(Mem_WB_Des_Reg), .eq(comparator_1_eq));  // open: gt, lt
  Comparator #(.width(4)) comparator_2 (.a(Mem_WB_Des_Reg), .b(4'b0000), .gt(comparator_2_gt));  // open: eq, lt
  and and_1 (Load_Store_Hazard, EX_Mem_MW, comparator_1_eq, Mem_WB_MR, comparator_2_gt);
endmodule
