// Logisim project Load-Use-Hazard-detection.circ as structural Verilog: 2 circuits, main circuit main
module main (
);

  Hazrd_Detection_Unit hazrd_detection_unit_1 ();  // open: ID_EX_MemRead, IF_ID_rs, LW_Hazard, ID_EX_rt, IF_ID_rt, IF_ID_MemWrite
endmodule

module Hazrd_Detection_Unit (
  input  ID_EX_MemRead,
  input  IF_ID_MemWrite,
  input  [3:0] IF_ID_rs,
  input  [3:0] ID_EX_rt,
  input  [3:0] IF_ID_rt,
  output LW_Hazard
);

  wire comparator_1_eq, comparator_2_eq, not_1_out, or_1_out;

  not not_1 (not_1_out, IF_ID_MemWrite);
  Comparator #(.width(4), .mode("unsigned")) comparator_1 (
    .a(IF_ID_rs), .b(ID_EX_rt), .eq(comparator_1_eq));  // open: gt, lt
  Comparator #(.width(4), .mode("unsigned")) comparator_2 (
    .a(ID_EX_rt), .b(IF_ID_rt), .eq(comparator_2_eq));  // open: gt, lt
  or or_1 (or_1_out, comparator_1_eq, comparator_2_eq);
  and and_1 (LW_Hazard, ID_EX_MemRead, not_1_out, or_1_out);
endmodule
