// Logisim project MEM-WB.circ as structural Verilog: 1 circuit, main circuit main
module main (
  input  Enable_Register,
  input  MTR_inp,
  input  RW_inp,
  input  MR_inp,
  input  [7:0] Read_Data_Stack_inp,
  input  [7:0] ALU_Res_inp,
  input  [7:0] Read_Data_inp,
  input  [3:0] Des_Reg_inp,
  input  sp_in,
  input  CLK,
  input  CLR,
  output MTR_out,
  output RW_out,
  output MR_out,
  output [7:0] Read_Data_Stack_out,
  output [7:0] ALU_Res_out,
  output [7:0] Read_Data_out,
  output [3:0] Des_Reg_out,
  output sp_out
);

  Register #(.width(1)) MTR (.D(MTR_inp), .en(Enable_Register), .Q(MTR_out), .clk(CLK), .clr(CLR));
  Register #(.width(1)) RW (.D(RW_inp), .en(Enable_Register), .Q(RW_out), .clk(CLK), .clr(CLR));
  Register #(.width(1)) RW_2 (.D(MR_inp), .en(Enable_Register), .Q(MR_out), .clk(CLK), .clr(CLR));
  Register Read_Data_Stack (
    .D(Read_Data_Stack_inp), .en(Enable_Register), .Q(Read_Data_Stack_out), .clk(CLK), .clr(CLR));
  Register ALU_Res (.D(ALU_Res_inp), .en(Enable_Register), .Q(ALU_Res_out), .clk(CLK), .clr(CLR));
  Register Read_Data (.D(Read_Data_inp), .en(Enable_Register), .Q(Read_Data_out), .clk(CLK), .clr(CLR));
  Register #(.width(4)) Des_reg (.D(Des_Reg_inp), .en(Enable_Register), .Q(Des_Reg_out), .clk(CLK), .clr(CLR));
  Register #(.width(1)) sp (.D(sp_in), .en(Enable_Register), .Q(sp_out), .clk(CLK), .clr(CLR));
endmodule
