// Logisim project MIPS pipelined.circ as structural Verilog: 2 circuits, main circuit test
module main (
  input  RESET,
  input  CLK,
  input  MemClear,
  output [2:0] out_4,
  output [7:0] PC_Value,
  output [7:0] out_6,
  output [7:0] Next_Inst,
  output [7:0] WriteData,
  output [7:0] MemData,
  output [19:0] Decoded_Ins,
  output [7:0] A,
  output [3:0] out_12,
  output [1:0] FrwrdA,
  output [7:0] out_14,
  output [7:0] WriteData_2,
  output [1:0] FrwrdB,
  output [7:0] B,
  output [1:0] FrwrdA_2,
  output [1:0] FrwrdB_2,
  output [7:0] FinalWriteData,
  output [1:0] ForwardA,
  output [1:0] ForwardB
);

  wire ALUSrc, ALUSrcCtrl, beq_ctrl, bneq_ctrl, comparator_1_eq, CtrlRW, EX_MEM_beq, EX_MEM_bneq,
       EX_MEM_jumpCtrl, EX_MEM_MR, EX_MEM_MTR, EX_MEM_MW, EX_MEM_RW, ID_EX_beq, ID_EX_bneq, ID_EX_JumpCtrl,
       ID_EX_MemRead, ID_EX_MemWrite, ID_EX_MTR, ID_EX_RW, ID_EX_ShiftCtrl, IF_ID_MW_LW, IF_ID_RW_LW,
       JumpCtrl, LoadUseHazard, LSHazard, MEM_WB_MR, MEM_WB_RW, MemRead_ctrl, MemToReg, MemToRegCtrl,
       MemWrite_Ctrl, multiplexer_7_out, n7408_1_p3, n7408_1_p6, not_1_out, not_2_out, not_3_out, not_4_out,
       PC_Src, Reg_Des, ShiftControl, ST_Load, ST_out1, ST_out2, ST_out3, ST_Store, StackMR, StackMW, ZFlag,
       ZFlag_out;
  wire [2:0] ALU_OP;
  wire [3:0] Dst_Reg, DstReg, EX_MEM_DstReg, ID_EX_DstReg, ID_EX_SrcReg1, ID_EX_SrcReg2,
       instructionsplitter_1_shiftamnt, OpCode, SrcReg1, SrcReg2;
  wire [7:0] Address_Imm, Address_Imm_out, ALURES_out2, Branch_in, Branch_out, data1, data2_t, Data_Mem_Data,
       EM_MEM_JumpAddr, EX_MEM_ALURES, EX_MEM_WriteData, Final_Address, ID_EX_data1, ID_EX_data2,
       ID_EX_jumpAddr, ID_EX_WriteData, JumpAddrIn, MEM_WB_WriteData, multiplexer_2_out, multiplexer_3_out,
       multiplexer_4_out, multiplexer_5_out, multiplexer_8_out, multiplexer_11_out, multiplexer_12_out,
       multiplexer_16_out, PC_4_EX_MEM, PC_4_ID_EX, PC_4_out1, PC___1___Address, shiftAmnt, shiftAmnt_out,
       StackData, StackDataOut;
  wire [19:0] MIPS_inst_in, MIPS_inst_out;

  Multiplexer #(.width(8), .enable("false")) multiplexer_1 (
    .in0(out_6), .in1(Final_Address), .out(Next_Inst), .sel(PC_Src));
  not not_1 (not_1_out, LoadUseHazard);
  Multiplexer #(.width(8), .enable("false")) multiplexer_2 (
    .in0(Data_Mem_Data), .in1(StackData), .out(multiplexer_2_out), .sel(ST_out2));
  Multiplexer #(.width(8), .enable("false")) multiplexer_3 (
    .in0(EX_MEM_ALURES), .in1(multiplexer_2_out), .out(multiplexer_3_out), .sel(EX_MEM_MTR));
  instruction_memory_main main_1 (
    .PC_Value(Next_Inst), .Reset(RESET), .Clock(CLK), .PC_Value_2(PC_Value), .MIPS_Instruction(Decoded_Ins),
    .in_2(not_1_out));
  // Probe on Decoded_Ins
  Multiplexer #(.select(2), .width(8), .enable("false")) multiplexer_4 (
    .in0(data1), .in1(multiplexer_3_out), .in2(out_14), .out(multiplexer_4_out), .sel(ForwardA));  // open: in3
  Multiplexer #(.select(2), .width(8), .enable("false")) multiplexer_5 (
    .in0(data2_t), .in1(multiplexer_3_out), .in2(out_14), .out(multiplexer_5_out), .sel(ForwardB));  // open: in3
  Adder adder_1 (.a(8'h1), .b(PC_Value), .out(out_6));  // open: cin, cout
  Multiplexer #(.width(20), .enable("false")) multiplexer_6 (
    .in0(Decoded_Ins), .in1(20'h70000), .out(MIPS_inst_in), .sel(PC_Src));
  Branch_Hazard branch_hazard_1 (
    .IF_ID_Src_Reg_1(SrcReg1), .IF_ID_BQE(beq_ctrl), .IF_ID_BNE(bneq_ctrl), .ID_EX_Des_Reg(ID_EX_DstReg),
    .EX_Mem_Des_Reg(EX_MEM_DstReg), .IF_ID_Src_Reg_2(SrcReg2), .Forward_A1(ForwardA[1]),
    .Forward_A0(ForwardA[0]), .Forward_B1(ForwardB[1]), .Forward_B0(ForwardB[0]));  // open: Branch_Stall
  // Probe on multiplexer_4_out
  // Probe on multiplexer_5_out
  IF_ID_main main_2 (
    .PC_input(out_6), .PC_output(PC_4_out1), .Mips_Instructions(MIPS_inst_in),
    .Mips_Instructions_Output(MIPS_inst_out), .Enable_Change(1'b1), .CLK(CLK), .CLR(RESET));
  // Probe on PC___1___Address
  // Probe on PC_4_out1
  Multiplexer #(.enable("false")) multiplexer_7 (
    .in0(bneq_ctrl), .in1(beq_ctrl), .out(multiplexer_7_out), .sel(comparator_1_eq));
  Comparator comparator_1 (.a(multiplexer_4_out), .b(multiplexer_5_out), .eq(comparator_1_eq));  // open: gt, lt
  Multiplexer #(.width(8), .enable("false")) multiplexer_8 (
    .in0(PC_4_out1), .in1(PC___1___Address), .out(multiplexer_8_out), .sel(multiplexer_7_out));
  Adder adder_2 (.a(PC_4_out1), .b(Address_Imm), .out(PC___1___Address));  // open: cin, cout
  StackLogic stacklogic_1 (
    .Source_Reg_1(SrcReg1), .Source_Reg_2(SrcReg2), .Load_Stack(ST_Load), .Store_Stack(ST_Store));
  // Probe on Final_Address
  Multiplexer #(.width(8), .enable("false")) multiplexer_9 (
    .in0(multiplexer_8_out), .in1(JumpAddrIn), .out(Final_Address), .sel(JumpCtrl));
  InstructionSplitter instructionsplitter_1 (
    .in_1(MIPS_inst_out), .ShiftAmnt(instructionsplitter_1_shiftamnt), .Dst_Reg(DstReg), .Src_Reg_2(SrcReg2),
    .Src_Reg_1(SrcReg1), .OpCode(OpCode), .Address___imme(Address_Imm), .Target_Jump_addr(JumpAddrIn));
  or or_1 (PC_Src, JumpCtrl, multiplexer_7_out);
  assign shiftAmnt = {{4{1'b0}}, instructionsplitter_1_shiftamnt};  // Bit_Extender bit_extender_1
  Multiplexer #(.width(4), .enable("false")) multiplexer_10 (.in0(SrcReg2), .in1(DstReg), .out(Dst_Reg), .sel(Reg_Des));
  control_unit_main main_3 (
    .Opcode(OpCode), .Shift(ShiftControl), .ALU_OP(out_4), .Reg_Des(Reg_Des), .ALU_Src(ALUSrcCtrl),
    .MemToReg(MemToRegCtrl), .RegWrite(CtrlRW), .beq(beq_ctrl), .bneq(bneq_ctrl), .Mem_Write(MemWrite_Ctrl),
    .Mem_Read(MemRead_ctrl), .Jump(JumpCtrl));
  not not_2 (not_2_out, CLK);
  regFileCopy regfilecopy_1 (
    .Src_Reg_1(SrcReg1), .Dst_Reg(out_12), .Src_Reg_2(SrcReg2), .Read_Data_1(data1), .Read_Data_2(data2_t),
    .Reg_Write(MEM_WB_RW), .CLK(not_2_out), .Clear(RESET), .Write_Data(WriteData));
  Load_Store_Hazard load_store_hazard_1 (
    .EX_Mem_MW(EX_MEM_MW), .Ex_Mem_Des_Reg(EX_MEM_DstReg), .Mem_WB_Des_Reg(out_12), .Mem_WB_MR(MEM_WB_MR),
    .Load_Store_Hazard(LSHazard));
  Hazrd_Detection_Unit hazrd_detection_unit_1 (
    .ID_EX_MemRead(ID_EX_MemRead), .IF_ID_rs(SrcReg1), .LW_Hazard(LoadUseHazard), .ID_EX_rt(ID_EX_DstReg),
    .IF_ID_rt(SrcReg2));  // open: IF_ID_MemWrite
  ID_EX id_ex_1 (
    .PC_input(PC_4_out1), .Target_Address_inp(JumpAddrIn), .ALU_src_inp(ALUSrcCtrl), .MTR_in(MemToRegCtrl),
    .RW_in(IF_ID_RW_LW), .BNEQ_in(bneq_ctrl), .BEQ_in(beq_ctrl), .MW_in(IF_ID_MW_LW), .MR_in(MemRead_ctrl),
    .jump_in(JumpCtrl), .shift_in(ShiftControl), .Data_1_inp(data1), .Data_2_inp(data2_t),
    .SRC_Reg_1_inp(SrcReg1), .Src_Reg_2_inp(SrcReg2), .Address_inp(Address_Imm), .Shift_amt_inp(shiftAmnt),
    .Des_Reg_inp(Dst_Reg), .sp_in(ST_Load), .PC_output(PC_4_ID_EX), .Target_Address_Output(ID_EX_jumpAddr),
    .ALUop(ALU_OP), .ALUSrc(ALUSrc), .MemToReg(ID_EX_MTR), .RegWrite(ID_EX_RW), .bneq(ID_EX_bneq),
    .beq(ID_EX_beq), .MemWrite(ID_EX_MemWrite), .MemRead(ID_EX_MemRead), .jump(ID_EX_JumpCtrl),
    .shiftAmnt(ID_EX_ShiftCtrl), .Data_1_out(ID_EX_data1), .Data_2_out(ID_EX_data2),
    .Src_Reg_1_out(ID_EX_SrcReg1), .Src_Reg_2_out(ID_EX_SrcReg2), .Addr_Imme(Address_Imm_out),
    .Shift_amt_out(shiftAmnt_out), .Des_Reg_out(ID_EX_DstReg), .sp(ST_out1), .Enable_operation(1'b1),
    .CLK(CLK), .CLR(RESET), .ALU_op_in(out_4));
  Multiplexer #(.select(2), .width(8), .enable("false")) multiplexer_11 (
    .in0(ID_EX_data1), .in1(WriteData), .in2(EX_MEM_ALURES), .out(multiplexer_11_out), .sel(FrwrdA));  // open: in3
  Multiplexer #(.select(2), .width(8), .enable("false")) multiplexer_12 (
    .in0(ID_EX_data2), .in1(WriteData), .in2(EX_MEM_ALURES), .out(multiplexer_12_out), .sel(FrwrdB));  // open: in3
  Multiplexer #(.enable("false")) multiplexer_13 (
    .in0(MemWrite_Ctrl), .in1(1'b0), .out(IF_ID_MW_LW), .sel(LoadUseHazard));
  Multiplexer #(.enable("false")) multiplexer_14 (.in0(CtrlRW), .in1(1'b0), .out(IF_ID_RW_LW), .sel(LoadUseHazard));
  Multiplexer #(.width(8), .enable("false")) multiplexer_15 (
    .in0(EX_MEM_WriteData), .in1(WriteData), .out(FinalWriteData), .sel(LSHazard));
  Adder adder_3 (.a(PC_4_ID_EX), .b(Address_Imm_out), .out(Branch_in));  // open: cin, cout
  Multiplexer #(.select(3), .width(8), .enable("false")) multiplexer_16 (
    .in0(multiplexer_11_out), .in1(multiplexer_11_out), .in2(multiplexer_11_out), .in3(multiplexer_11_out),
    .in4(multiplexer_11_out), .in5(multiplexer_12_out), .in6(multiplexer_12_out), .in7(multiplexer_11_out),
    .out(multiplexer_16_out), .sel(ALU_OP));
  Multiplexer #(.select(3), .width(8), .enable("false")) multiplexer_17 (
    .in0(multiplexer_12_out), .in1(multiplexer_12_out), .in2(multiplexer_12_out), .in3(multiplexer_12_out),
    .in4(multiplexer_12_out), .in5(multiplexer_11_out), .in6(multiplexer_11_out), .in7(multiplexer_12_out),
    .out(ID_EX_WriteData), .sel(ALU_OP));
  Multiplexer #(.width(8), .enable("false")) multiplexer_18 (
    .in0(multiplexer_16_out), .in1(shiftAmnt_out), .out(A), .sel(ID_EX_ShiftCtrl));
  Multiplexer #(.width(8), .enable("false")) multiplexer_19 (
    .in0(ID_EX_WriteData), .in1(Address_Imm_out), .out(B), .sel(ALUSrc));
  // ALU_8_by_ART alu_8_by_art_1: pin names not known; wires that end beside it: A, B, ALU_OP, ZFlag, out_14
  EX_MEM_main main_4 (
    .PC_inp(PC_4_ID_EX), .Branch_inp(Branch_in), .jump_inp(ID_EX_JumpCtrl), .Target_inp(ID_EX_jumpAddr),
    .MTR_inp(ID_EX_MTR), .RW_inp(ID_EX_RW), .Bneq_in(ID_EX_bneq), .Beq_in(ID_EX_beq), .MW_in(ID_EX_MemWrite),
    .MR_in(ID_EX_MemRead), .Zero_in(ZFlag), .Result_inp(out_14), .Write_Data_inp(ID_EX_WriteData),
    .Des_Reg_inp(ID_EX_DstReg), .sp_in(ST_out1), .PC_out(PC_4_EX_MEM), .Branch_out(Branch_out),
    .jump_out(EX_MEM_jumpCtrl), .Target_out(EM_MEM_JumpAddr), .MTR_out(EX_MEM_MTR), .RW_out(EX_MEM_RW),
    .Bneq_out(EX_MEM_bneq), .Beq_out(EX_MEM_beq), .MW_out(EX_MEM_MW), .MR_out(EX_MEM_MR),
    .Zero_out(ZFlag_out), .Result_out(EX_MEM_ALURES), .Write_Data_out(EX_MEM_WriteData),
    .Des_Reg_out(EX_MEM_DstReg), .sp_out(ST_out2), .Enable_Register(1'b1), .CLK(CLK), .CLR(RESET));
  Forwarding_Unit forwarding_unit_1 (
    .ID_EX_Src_Reg_1(ID_EX_SrcReg1), .EX_Mem_Reg_Write(EX_MEM_RW), .EX_Mem_Des_Reg(EX_MEM_DstReg),
    .Mem_WB_Des_Reg(out_12), .Mem_WB_Reg_Write(MEM_WB_RW), .ID_EX_Src_Reg_2(ID_EX_SrcReg2),
    .ForwardA(FrwrdA), .ForwardB(FrwrdB));
  stack_memory_main main_5 (
    .Address(EX_MEM_ALURES), .WriteData(FinalWriteData), .MW(StackMW), .MR(StackMR), .Clear(RESET),
    .CLK(CLK), .out_7(StackData));
  not not_3 (not_3_out, ST_out2);
  not not_4 (not_4_out, ST_out2);
  DataMem datamem_1 (
    .Address(EX_MEM_ALURES), .WriteData(FinalWriteData), .MW(n7408_1_p3), .MR(n7408_1_p6), .Clear(RESET),
    .CLK(CLK), .out_7(Data_Mem_Data));
  // _7408 7408_1: pin names not known; wires that end beside it: EX_MEM_MW, not_3_out, n7408_1_p3, not_4_out, EX_MEM_MR, n7408_1_p6, EX_MEM_MW, ST_out2, StackMW, ST_out2, EX_MEM_MR, StackMR
  MEM_WB_main main_6 (
    .MTR_inp(EX_MEM_MTR), .RW_inp(EX_MEM_RW), .Read_Data_Stack_inp(StackData), .ALU_Res_inp(EX_MEM_ALURES),
    .Read_Data_inp(Data_Mem_Data), .Des_Reg_inp(EX_MEM_DstReg), .sp_in(ST_out2), .MTR_out(MemToReg),
    .RW_out(MEM_WB_RW), .Read_Data_Stack_out(StackDataOut), .ALU_Res_out(ALURES_out2),
    .Read_Data_out(MEM_WB_WriteData), .Des_Reg_out(out_12), .sp_out(ST_out3), .Enable_Register(1'b1),
    .CLK(CLK), .CLR(RESET), .MR_inp(EX_MEM_MR), .MR_out(MEM_WB_MR));
  Multiplexer #(.width(8), .enable("false")) multiplexer_20 (
    .in0(MEM_WB_WriteData), .in1(StackDataOut), .out(MemData), .sel(ST_out3));
  Multiplexer #(.width(8), .enable("false")) multiplexer_21 (
    .in0(ALURES_out2), .in1(MemData), .out(WriteData), .sel(MemToReg));

  assign FrwrdA_2 = FrwrdA;
  assign FrwrdB_2 = FrwrdB;
  assign WriteData_2 = WriteData;

  // Other names for the same wires on the sheet: ALU_OP_Ctrl[2:0] = out_4; ALURES[7:0] = out_14;
  //   Branch_A1A0[1:0] = ForwardA; Branch_B1B0[1:0] = ForwardB; CorrectWriteData[7:0] = FinalWriteData;
  //   ForwardA_t[1:0] = FrwrdA; ForwardB_t[1:0] = FrwrdB; main_reset = RESET; MemClear_t = RESET;
  //   MEM_WB_DstReg[3:0] = out_12; PC_4_in[7:0] = out_6

  // Notes on the sheet:
  //   IF
  //   choosing the right data 
  //   Branch Hazard Handler (in ID)
  //   Calc Target Addr
  //   ID
  //   EX
  //   MEM
  //   WB
endmodule

module test (
  input  [7:0] in_1,
  input  [7:0] in_2,
  input  [2:0] in_3,
  output [7:0] out_4
);

  // ALU_8_by_ART alu_8_by_art_1: pin names not known; wires that end beside it: in_1, in_2, in_3, out_4
endmodule
