// Logisim project MIPS.circ as structural Verilog: 2 circuits, main circuit test
module main (
  input  RESET,
  input  CLK,
  input  MemClear,
  input  CLEAR,
  output [2:0] out_5,
  output [7:0] PC_Value,
  output [7:0] Next_Inst,
  output [7:0] A,
  output [7:0] WriteData,
  output [7:0] out_10,
  output [19:0] Decoded_Ins,
  output [7:0] MemData,
  output [7:0] B,
  output [7:0] WriteData_2
);

  wire ALUSrc, beq, bneq, brType, CtrlRW, JumpCtrl, MemRead, MemToReg, MemWrite, n7408_1_p3, n7408_1_p6,
       not_1_out, not_2_out, Reg_Des, ShiftControl, ST_Load, ST_Store, StackMR, StackMW, ZFlag;
  wire [3:0] DstReg, instructionsplitter_1_shiftamnt, multiplexer_1_out, OpCode, SrcReg1, SrcReg2;
  wire [7:0] adder_2_out, Address_Imm, Data2, datamem_1_out_7, JumpAddr, multiplexer_2_out,
       multiplexer_3_out, multiplexer_6_out, PC_4, regfilecopy_1_read_data_1, shiftAmnt, StackData;

  instruction_memory_main main_1 (
    .PC_Value(Next_Inst), .Reset(RESET), .Clock(CLK), .PC_Value_2(PC_Value), .MIPS_Instruction(Decoded_Ins));  // open: in_2
  Adder adder_1 (.a(8'h1), .b(PC_Value), .out(PC_4));  // open: cin, cout
  InstructionSplitter instructionsplitter_1 (
    .in_1(Decoded_Ins), .ShiftAmnt(instructionsplitter_1_shiftamnt), .Dst_Reg(DstReg), .Src_Reg_2(SrcReg2),
    .Src_Reg_1(SrcReg1), .OpCode(OpCode), .Address___imme(Address_Imm), .Target_Jump_addr(JumpAddr));
  // Probe on Decoded_Ins
  assign shiftAmnt = {{4{1'b0}}, instructionsplitter_1_shiftamnt};  // Bit_Extender bit_extender_1
  StackLogic stacklogic_1 (
    .Source_Reg_1(SrcReg1), .Source_Reg_2(SrcReg1), .Load_Stack(ST_Load), .Store_Stack(ST_Store));
  control_unit_main main_2 (
    .Opcode(OpCode), .Shift(ShiftControl), .ALU_OP(out_5), .Reg_Des(Reg_Des), .ALU_Src(ALUSrc),
    .MemToReg(MemToReg), .RegWrite(CtrlRW), .beq(beq), .bneq(bneq), .Mem_Write(MemWrite), .Mem_Read(MemRead),
    .Jump(JumpCtrl));
  Multiplexer #(.width(4), .enable("false")) multiplexer_1 (
    .in0(SrcReg2), .in1(DstReg), .out(multiplexer_1_out), .sel(Reg_Des));
  regFileCopy regfilecopy_1 (
    .Src_Reg_1(SrcReg1), .Dst_Reg(multiplexer_1_out), .Src_Reg_2(SrcReg2),
    .Read_Data_1(regfilecopy_1_read_data_1), .Read_Data_2(Data2), .Reg_Write(CtrlRW), .CLK(CLK),
    .Clear(CLEAR), .Write_Data(WriteData));
  Multiplexer #(.select(3), .width(8), .enable("false")) multiplexer_2 (
    .in0(regfilecopy_1_read_data_1), .in1(regfilecopy_1_read_data_1), .in2(regfilecopy_1_read_data_1),
    .in3(regfilecopy_1_read_data_1), .in4(regfilecopy_1_read_data_1), .in5(Data2), .in6(Data2),
    .in7(regfilecopy_1_read_data_1), .out(multiplexer_2_out), .sel(out_5));
  Multiplexer #(.select(3), .width(8), .enable("false")) multiplexer_3 (
    .in0(Data2), .in1(Data2), .in2(Data2), .in3(Data2), .in4(Data2), .in5(regfilecopy_1_read_data_1),
    .in6(regfilecopy_1_read_data_1), .in7(Data2), .out(multiplexer_3_out), .sel(out_5));
  Adder adder_2 (.a(PC_4), .b(Address_Imm), .out(adder_2_out));  // open: cin, cout
  Multiplexer #(.width(8), .enable("false")) multiplexer_4 (
    .in0(multiplexer_2_out), .in1(shiftAmnt), .out(A), .sel(ShiftControl));
  Multiplexer #(.width(8), .enable("false")) multiplexer_5 (
    .in0(multiplexer_3_out), .in1(Address_Imm), .out(B), .sel(ALUSrc));
  Multiplexer #(.width(8), .enable("false")) multiplexer_6 (
    .in0(PC_4), .in1(adder_2_out), .out(multiplexer_6_out), .sel(brType));
  Multiplexer #(.enable("false")) multiplexer_7 (.in0(bneq), .in1(beq), .out(brType), .sel(ZFlag));
  // ALU_8_by_ART alu_8_by_art_1: pin names not known; wires that end beside it: A, B, out_5, ZFlag, out_10
  Multiplexer #(.width(8), .enable("false")) multiplexer_8 (
    .in0(multiplexer_6_out), .in1(JumpAddr), .out(Next_Inst), .sel(JumpCtrl));
  stack_memory_main main_3 (
    .Address(out_10), .WriteData(Data2), .MW(StackMW), .MR(StackMR), .Clear(MemClear), .CLK(CLK),
    .out_7(StackData));
  not not_1 (not_1_out, ST_Store);
  not not_2 (not_2_out, ST_Load);
  DataMem datamem_1 (
    .Address(out_10), .WriteData(Data2), .MW(n7408_1_p3), .MR(n7408_1_p6), .Clear(MemClear), .CLK(CLK),
    .out_7(datamem_1_out_7));
  // _7408 7408_1: pin names not known; wires that end beside it: MemWrite, not_1_out, n7408_1_p3, not_2_out, MemRead, n7408_1_p6, MemWrite, ST_Store, StackMW, ST_Load, MemRead, StackMR
  Multiplexer #(.width(8), .enable("false")) multiplexer_9 (
    .in0(datamem_1_out_7), .in1(StackData), .out(MemData), .sel(ST_Load));
  Multiplexer #(.width(8), .enable("false")) multiplexer_10 (
    .in0(out_10), .in1(MemData), .out(WriteData), .sel(MemToReg));

  assign WriteData_2 = WriteData;

  // Other names for the same wires on the sheet: ALU_OP[2:0] = out_5; ALURES[7:0] = out_10; NextIns[7:0] = Next_Inst
endmodule

module test (
  input  [7:0] in_1,
  input  [7:0] in_2,
  input  [2:0] in_3,
  input  [3:0] in_4,
  output [7:0] out_5,
  output [3:0] out_6
);

  wire clock_1_out;

  // ALU_8_by_ART alu_8_by_art_1: pin names not known; wires that end beside it: in_1, in_2, in_3, out_5
  Clock clock_1 (.out(clock_1_out));
  Register #(.width(4)) register_1 (.D(in_4), .Q(out_6), .clk(clock_1_out));  // open: en, clr
endmodule
