// Logisim project Register File.circ as structural Verilog: 2 circuits, main circuit main
module main (
);

  regFileCopy regfilecopy_1 ();  // open: Src_Reg_1, Dst_Reg, Src_Reg_2, Read_Data_1, Read_Data_2, Reg_Write, CLK, Clear, Write_Data
endmodule

module regFileCopy (
  input  [3:0] Src_Reg_1,
  input  [3:0] Dst_Reg,
  input  [3:0] Src_Reg_2,
  input  [7:0] Write_Data,
  input  Reg_Write,
  input  CLK,
  input  Clear,
  output [7:0] Read_Data_1,
  output [7:0] Read_Data_2
);

  wire and_1_out, and_2_out, and_3_out, and_4_out, and_5_out, and_6_out, and_7_out, and_8_out,
       decoder_1_out0, decoder_1_out1, decoder_1_out2, decoder_1_out3, decoder_1_out4, decoder_1_out5,
       decoder_1_out6, decoder_1_out7;
  wire [7:0] multiplexer_1_out, sp_q, t0_q, t1_q, t2_q, t3_q, t4_q, t5_q, zero_q;

  Decoder #(.select(4), .enable("false")) decoder_1 (
    .out0(decoder_1_out0), .out1(decoder_1_out1), .out2(decoder_1_out2), .out3(decoder_1_out3),
    .out4(decoder_1_out4), .out5(decoder_1_out5), .out6(decoder_1_out6), .out7(decoder_1_out7), .sel(Dst_Reg));  // open: out8, out9, out10, out11, out12, out13, out14, out15
  and and_1 (and_1_out, decoder_1_out0, 1'b0);
  and and_2 (and_2_out, decoder_1_out1, Reg_Write);
  and and_3 (and_3_out, decoder_1_out2, Reg_Write);
  and and_4 (and_4_out, decoder_1_out3, Reg_Write);
  and and_5 (and_5_out, decoder_1_out4, Reg_Write);
  and and_6 (and_6_out, decoder_1_out5, Reg_Write);
  and and_7 (and_7_out, decoder_1_out6, Reg_Write);
  and and_8 (and_8_out, decoder_1_out7, Reg_Write);
  Multiplexer #(.width(8), .enable("false")) multiplexer_1 (
    .in0(Write_Data), .in1({8{1'b1}}), .out(multiplexer_1_out), .sel(Clear));
  Register zero (.D(Write_Data), .en(and_1_out), .Q(zero_q), .clk(CLK), .clr(Clear));
  Register t0 (.D(Write_Data), .en(and_2_out), .Q(t0_q), .clk(CLK), .clr(Clear));
  Register t1 (.D(Write_Data), .en(and_3_out), .Q(t1_q), .clk(CLK), .clr(Clear));
  Register t2 (.D(Write_Data), .en(and_4_out), .Q(t2_q), .clk(CLK), .clr(Clear));
  Register t3 (.D(Write_Data), .en(and_5_out), .Q(t3_q), .clk(CLK), .clr(Clear));
  Register t4 (.D(Write_Data), .en(and_6_out), .Q(t4_q), .clk(CLK), .clr(Clear));
  Register t5 (.D(Write_Data), .en(and_7_out), .Q(t5_q), .clk(CLK), .clr(Clear));
  Register sp (.D(multiplexer_1_out), .en(and_8_out), .Q(sp_q), .clk(CLK), .clr(Clear));
  Multiplexer #(.select(4), .width(8), .enable("false")) multiplexer_2 (
    .in0(zero_q), .in1(t0_q), .in2(t1_q), .in3(t2_q), .in4(t3_q), .in5(t4_q), .in6(t5_q), .in7(sp_q),
    .out(Read_Data_1), .sel(Src_Reg_1));  // open: in8, in9, in10, in11, in12, in13, in14, in15
  Multiplexer #(.select(4), .width(8), .enable("false")) multiplexer_3 (
    .in0(zero_q), .in1(t0_q), .in2(t1_q), .in3(t2_q), .in4(t3_q), .in5(t4_q), .in6(t5_q), .in7(sp_q),
    .out(Read_Data_2), .sel(Src_Reg_2));  // open: in8, in9, in10, in11, in12, in13, in14, in15
endmodule
