// Logisim project StackLogic.circ as structural Verilog: 2 circuits, main circuit main
module main (
  input  [3:0] in_1,
  input  [3:0] in_2
);

  wire stacklogic_1_load_stack, stacklogic_1_store_stack;

  StackLogic stacklogic_1 (
    .Source_Reg_1(in_1), .Source_Reg_2(in_2), .Load_Stack(stacklogic_1_load_stack),
    .Store_Stack(stacklogic_1_store_stack));
endmodule

module StackLogic (
  input  [3:0] Source_Reg_1,
  input  [3:0] Source_Reg_2,
  output Load_Stack,
  output Store_Stack
);

  wire not_1_out, not_2_out;

  not not_1 (not_1_out, Source_Reg_1[3]);
  not not_2 (not_2_out, Source_Reg_2[3]);
  and and_1 (Load_Stack, not_1_out, Source_Reg_1[2], Source_Reg_1[1], Source_Reg_1[0]);
  and and_2 (Store_Stack, not_2_out, Source_Reg_2[2], Source_Reg_2[1], Source_Reg_2[0]);
endmodule
