// Logisim project control_unit.circ as structural Verilog: 2 circuits, main circuit main
module main (
  input  [3:0] Opcode,
  output Shift,
  output [2:0] ALU_OP,
  output Reg_Des,
  output ALU_Src,
  output MemToReg,
  output RegWrite,
  output beq,
  output bneq,
  output Mem_Write,
  output Mem_Read,
  output Jump
);

  wire [3:1] rom_1_data;

  ROM #(.addrWidth(4), .dataWidth(16)) rom_1 (
    .addr(Opcode),
    .data({Jump, Mem_Read, Mem_Write, bneq, beq, RegWrite, MemToReg, ALU_Src, Reg_Des, ALU_OP, rom_1_data, Shift}),
    .sel(1'b1));

  // Notes on the sheet:
  //   contents of rom_1 (hex, n*v repeats v):
  //   510 1010 2100 810 480 520 4e1 4700 8000 4a0 4c0 530 490 480 500 4d1
endmodule

module control_unit (
);

  main main_1 ();  // open: Opcode, Shift, ALU_OP, Reg_Des, ALU_Src, MemToReg, RegWrite, beq, bneq, Mem_Write, Mem_Read, Jump
endmodule
