// Logisim project instruction_memory.circ as structural Verilog: 2 circuits, main circuit main
module main (
  input  [7:0] PC_Value,
  input  in_2,
  input  Reset,
  input  Clock,
  output [7:0] PC_Value_2,
  output [19:0] MIPS_Instruction
);

  Register PC (.D(PC_Value), .en(in_2), .Q(PC_Value_2), .clk(Clock), .clr(Reset));
  ROM #(.dataWidth(20)) rom_1 (.addr(PC_Value_2), .data(MIPS_Instruction), .sel(in_2));

  // Notes on the sheet:
  //   contents of rom_1 (hex, n*v repeats v):
  //   e020a e0305 42310 41340 44150 23203 f2021 32401 81500 c5150 2202 64041 73203 d2410 91530 81400 51105
  //   b3314 a3330 81500 113fb
endmodule

module instruction_memory (
);

  main main_1 ();  // open: PC_Value, Reset, Clock, PC_Value_2, MIPS_Instruction, in_2
endmodule
